# Fritzing sketch Fritzing Sketch with perfboard (saved by Fritzing 0.9.3b)
perfboards: 1

parts:
  Onderdeel1 = Arduino Nano (Rev3.0)
  ZS-042_RTC1 = ZS-042 RTC Module
  J1 = Piezo Speaker
  R3 = Resistor [tolerance=±5% resistance=10k package="0805 [SMD]"]
  Q1 = NPN-Transistor [package="TO92 [THT]"]
  S2 = Pushbutton [package="[THT]"]
  S3 = Pushbutton [package="[THT]"]
  R5 = Rotary Potentiometer (Small) [maximum_resistance=100kΩ package=THT]
  Onderdeel2 = Arduino Nano (Rev3.0)  # not connected
  J3 = Power Jack [part_number="5V 1000mA input" package=power_jack_smd]  # not connected
  Q4 = NPN-Transistor [package="TO92 [THT]"]  # not connected
  Q5 = NPN-Transistor [package="TO92 [THT]"]  # not connected
  Grove2 = Grove 4 Digit Display  # not connected
  R9 = Resistor [tolerance=±5% resistance=10k package="0805 [SMD]"]  # not connected
  LED3 = smd LED [color="Green (555nm)" package="0805 [SMD]"]  # not connected
  R10 = Resistor [tolerance=±5% resistance=100 package="0805 [SMD]"]  # not connected
  R11 = Resistor [tolerance=±5% resistance=10k package="0805 [SMD]"]  # not connected
  LED4 = smd LED [color="Red (633nm)" package="0805 [SMD]"]  # not connected
  S4 = Round Pushbutton  # not connected
  R13 = Resistor [tolerance=±5% resistance=100 package="0805 [SMD]"]  # not connected
  R14 = Resistor [tolerance=±5% resistance=10k package="0805 [SMD]"]  # not connected
  ZS-042_RTC2 = ZS-042 RTC Module  # not connected
  Q6 = NPN-Transistor [package="TO92 [THT]"]  # not connected
  R15 = Resistor [tolerance=±5% resistance=10k package="0805 [SMD]"]  # not connected
  J4 = Piezo Speaker
  R16 = Rotary Potentiometer (Small) [maximum_resistance=100kΩ package=THT]
  S5 = Pushbutton [package="[THT]"]
  S6 = Pushbutton [package="[THT]"]

nets:
  N1: Onderdeel1.D4, R3.Pin_1
  N2: Onderdeel1.A5, ZS-042_RTC1.SCL
  N3: Onderdeel1.A4, ZS-042_RTC1.SDA
  N4: Onderdeel1.A1, S3.Pin_3, S3.Pin_4
  N5: Onderdeel1.A0, S2.Pin_3, S2.Pin_4
  N6: J1.pin1, Q1.E
  N7: J1.pin2, R5.leg1
  N8: R3.Pin_0, Q1.B
  N9: J4.pin2, R16.leg1
  N10: S5.Pin_3, S5.Pin_4
  N11: S6.Pin_3, S6.Pin_4

notes:
  Input: 12V 1A
  Project: AIR-K.O.
  Sketch version: 0.04 ALPHA
  Sketch date: 7-7-2019
  https://github.com/SANCLA/AIR-KO
  10 kΩ
  HOUR
  MINUTE
  2N2222
