# Fritzing sketch Fritzing Sketch (saved by Fritzing 0.9.3b)

parts:
  Onderdeel1 = Arduino Nano (Rev3.0)
  S1 = Round Pushbutton
  ZS-042_RTC1 = ZS-042 RTC Module
  R1 = Resistor [tolerance=±5% resistance=10k package="0805 [SMD]"]
  LED1 = smd LED [color="Red (633nm)" package="0805 [SMD]"]
  J1 = Piezo Speaker
  R3 = Resistor [tolerance=±5% resistance=10k package="0805 [SMD]"]
  Grove1 = Grove 4 Digit Display  # not connected
  J2 = Power Jack [part_number="5V 1000mA input" package=power_jack_smd]  # not connected
  C3 = Capacitor Polarized [package=cpol-radial-100uf-25v]  # not connected
  Q1 = NPN-Transistor [package="TO92 [THT]"]
  S2 = Pushbutton [package="[THT]"]
  S3 = Pushbutton [package="[THT]"]
  Q2 = NPN-Transistor [package="TO92 [THT]"]
  R4 = Resistor [tolerance=±5% resistance=100 package="0805 [SMD]"]
  R5 = Rotary Potentiometer (Small) [maximum_resistance=100kΩ package=THT]
  R6 = Resistor [tolerance=±5% resistance=10k package="0805 [SMD]"]
  LED2 = smd LED [color="Green (555nm)" package="0805 [SMD]"]
  Q3 = NPN-Transistor [package="TO92 [THT]"]
  R7 = Resistor [tolerance=±5% resistance=10k package="0805 [SMD]"]
  R8 = Resistor [tolerance=±5% resistance=100 package="0805 [SMD]"]

nets:
  N1: Onderdeel1.D4, R3.Pin_1
  N2: Onderdeel1.D5, R6.Pin_1
  N3: Onderdeel1.D6, S1.leg1
  N4: Onderdeel1.D10, R7.Pin_1
  N5: Onderdeel1.A5, ZS-042_RTC1.SCL
  N6: Onderdeel1.A4, ZS-042_RTC1.SDA
  N7: Onderdeel1.A1, S3.Pin_3, S3.Pin_4
  N8: Onderdeel1.A0, S2.Pin_3, S2.Pin_4
  N9: S1.leg0, R1.Pin_0
  N10: LED1.cathode, Q2.E
  N11: LED1.anode, R4.Pin_0
  N12: J1.pin1, Q1.E
  N13: J1.pin2, R5.leg1
  N14: R3.Pin_0, Q1.B
  N15: Q2.B, R6.Pin_0
  N16: LED2.cathode, Q3.E
  N17: LED2.anode, R8.Pin_0
  N18: Q3.B, R7.Pin_0

notes:
  Input: 5V 1A
  Project: AIR-K.O.
  Sketch version: 0.04 ALPHA
  Sketch date: 7-7-2019
  https://github.com/SANCLA/AIR-KO
  10kΩ
  100Ω
  10 kΩ
  100-1000 µF, 12 V
  HOUR
  MINUTE
  2N2222
